# Fritzing sketch LightWalker Arduino Mega Sketch (saved by Fritzing 0.8.3b)
breadboards: 1

parts:
  Part2 = Bluetooth Mate Silver
  Part3 = Triple Axis Accelerometer Breakout - ADXL345
  Part4 = Triple Axis Accelerometer Breakout - ADXL345
  Part5 = Triple Axis Accelerometer Breakout - ADXL345
  Part6 = Triple Axis Accelerometer Breakout - ADXL345
  Part7 = Arduino Mega 2560 (Rev3)
  Part9 = Breakout Board for Electret Microphone
  IC3 = MSGEQ7 [package=soic8]
  IC4 = DIP - 4 pins [chip_label=P9813 package="DIP (Dual Inline) [THT]"]
  IC5 = DIP - 24 pins [chip_label=TCA9548A package="DIP (Dual Inline) [THT]"]
  R1 = Resistor [tolerance=±5% resistance=220 package=THT]

nets:
  N1: Part2.RTS_5V, Part2.CTS_5V
  N2: Part2.RX_5V, Part7.D18/TX1
  N3: Part2.TX_5V, Part7.D19/RX1
  VCC: Part2.VCC, Part3.VCC, Part4.VCC, Part5.VCC, Part6.VCC, Part7.5V, IC3.VDD, IC3.CKIN, IC4.5v+, IC5.A2, IC5.Vcc, R1.Pin_1
  GND: Part2.GND, Part3.GND, Part4.GND, Part5.GND, Part6.GND, Part7.GND, Part9.GND, IC3.GND, IC3.CG, IC4.GND, IC5.A0, IC5.A1, IC5.GND
  N4: Part3.SDA, IC5.SD1
  N5: Part3.SCL, IC5.SC1
  N6: Part4.SDA, IC5.SD0
  N7: Part4.SCL, IC5.SC0
  N8: Part5.SDA, IC5.SD4
  N9: Part5.SCL, IC5.SC4
  N10: Part6.SDA, IC5.SD2
  N11: Part6.SCL, IC5.SC2
  N12: Part7.A1, IC3.DCOUT
  N13: Part7.SCL, IC5.SCL
  N14: Part7.SDA, IC5.SDA
  N15: Part7.RESET, IC3.RESET
  3V3: Part7.3V3, Part9.VCC
  N16: Part7.D4_PWM, IC3.STROBE
  N17: Part7.D51, IC4.data
  N18: Part7.D52, IC4.clock
  N19: Part9.AUD, IC3.AUDIO_IN
  N20: IC5.RESET, R1.Pin_0

custom parts:
  DIP - 4 pins: A DIP stand-in part for whatever IC you want. With 4 pins on a 300mil dual inline package (DIP) footprint.
  DIP - 24 pins: A DIP stand-in part for whatever IC you want. With 24 pins on a 300mil dual inline package (DIP) footprint.
