# Fritzing sketch LightWalker teensy3.0 Sketch - Copy (saved by Fritzing 0.8.3b)
circuit board: 16.9333cm x 5.64444cm
breadboards: 1

parts:
  BT = Bluetooth Mate Silver
  Part3 = Triple Axis Accelerometer Breakout - ADXL345
  Part4 = Triple Axis Accelerometer Breakout - ADXL345
  Part5 = Triple Axis Accelerometer Breakout - ADXL345
  Part6 = Triple Axis Accelerometer Breakout - ADXL345
  Mic = Breakout Board for Electret Microphone
  LEDS = DIP - 4 pins [chip_label=P9813 package="DIP (Dual Inline) [THT]"]
  IC5 = DIP - 24 pins [chip_label=TCA9548A package="DIP (Dual Inline) [THT]"]
  i2c_multiplex_RESET_R = Resistor [tolerance=±5% resistance=220 package=THT]
  Teensy_3_1 = Teensy 3.0
  LED_clock_R = Resistor [tolerance=±5% resistance=220 package=THT]
  LED_data_R = Resistor [tolerance=±5% resistance=220 package=THT]
  U1 = BATTERY-2 [package=battery-aaa]
  U2 = BATTERY-2 [package=battery-aaa]
  i2c_multiplex_SDA_Pullup_R = Resistor [tolerance=±5% resistance=4.7k package=THT]
  i2c_multiplex_SCL_pullup_R = Resistor [tolerance=±5% resistance=4.7k package=THT]

nets (from the breadboard view):
  N1: BT.RX_5V, Teensy_3_1.D1
  N2: BT.TX_5V, Teensy_3_1.D0
  VCC: BT.VCC, Part3.VCC, Part4.VCC, Part5.VCC, Part6.VCC, Mic.VCC, IC5.A2, IC5.Vcc, i2c_multiplex_RESET_R.Pin_1, Teensy_3_1.3V3, i2c_multiplex_SDA_Pullup_R.Pin_1, i2c_multiplex_SCL_pullup_R.Pin_1
  GND: BT.GND, Part3.GND, Part4.GND, Part5.GND, Part6.GND, Mic.GND, LEDS.GND, IC5.A0, IC5.A1, IC5.GND, Teensy_3_1.GND, U1.+1, U2.+1
  N3: Part3.SDA, IC5.SD1
  N4: Part3.SCL, IC5.SC1
  N5: Part4.SDA, IC5.SD0
  N6: Part4.SCL, IC5.SC0
  N7: Part5.SDA, IC5.SD3
  N8: Part5.SCL, IC5.SC3
  N9: Part6.SDA, IC5.SD2
  N10: Part6.SCL, IC5.SC2
  N11: Mic.AUD, Teensy_3_1.A0/D14
  N12: LEDS.5v+, U1.-1
  N13: LEDS.data, LED_data_R.Pin_0
  N14: LEDS.clock, LED_clock_R.Pin_0
  N15: IC5.RESET, i2c_multiplex_RESET_R.Pin_0
  N16: IC5.SCL, i2c_multiplex_SCL_pullup_R.Pin_0
  N17: IC5.SDA, Teensy_3_1.A4/D18, i2c_multiplex_SDA_Pullup_R.Pin_0
  N18: Teensy_3_1.D11, LED_data_R.Pin_1
  N19: Teensy_3_1.D13, LED_clock_R.Pin_1
  N20: Teensy_3_1.Vin, U2.-1

custom parts:
  DIP - 4 pins: A DIP stand-in part for whatever IC you want. With 4 pins on a 300mil dual inline package (DIP) footprint.
  DIP - 24 pins: A DIP stand-in part for whatever IC you want. With 24 pins on a 300mil dual inline package (DIP) footprint.
